// Logisim project RA.circ as structural Verilog: 5 circuits, main circuit Blatt_1_unsigned
module Blatt_1_unsigned (
  input  x2,
  input  x0,
  input  x3,
  input  x2_2,
  input  x1,
  input  x0_2,
  input  x3_2,
  input  x1_2,
  input  x0_3,
  input  x3_3,
  input  x0_4,
  input  x2_3,
  input  x2_4,
  input  x1_3,
  input  x3_4,
  input  x1_4,
  input  x0_5,
  input  x3_5,
  input  x1_5,
  input  x0_6,
  input  x3_6,
  input  x1_6,
  input  x2_5,
  output y0,
  output y3,
  output y1,
  output y2
);

  wire and_1_out, and_2_out, and_3_out, and_4_out, and_5_out, and_6_out, not_1_out, not_2_out, not_3_out,
       not_4_out, not_5_out, not_6_out;

  not not_1 (not_1_out, x2_3);
  not not_2 (not_2_out, x3_4);
  not not_3 (not_3_out, x0_5);
  not not_4 (not_4_out, x0_6);
  not not_5 (not_5_out, x2_5);
  not not_6 (not_6_out, x1_2);
  and and_1 (and_1_out, x3_2, not_6_out, x0_3);
  and and_2 (and_2_out, x3_3, x0_4, not_1_out);
  and and_3 (and_3_out, x2_4, x1_3, not_2_out);
  and and_4 (and_4_out, x1_4, not_3_out);
  and and_5 (and_5_out, x3_5, x1_5, not_4_out);
  and and_6 (and_6_out, x3_6, x1_6, not_5_out);
  or or_1 (y2, and_5_out, and_6_out);
  or or_2 (y1, and_1_out, and_2_out, and_3_out, and_4_out);
  and and_7 (y0, x2, x0);
  and and_8 (y3, x3, x2_2, x1, x0_2);
endmodule

module Blatt_1_signed (
  input  x1,
  input  x0,
  input  x3,
  input  x3_2,
  input  x2,
  input  x1_2,
  input  x3_3,
  input  x2_2,
  input  x1_3,
  input  x0_2,
  input  x1_4,
  input  x0_3,
  input  x3_4,
  input  x3_5,
  input  x2_3,
  input  x1_5,
  output out_17,
  output out_18
);

  wire and_1_out, and_2_out, and_3_out, and_4_out, and_5_out, not_1_out, not_2_out, not_3_out, not_4_out,
       not_5_out;

  not not_1 (not_1_out, x1);
  not not_2 (not_2_out, x3_2);
  not not_3 (not_3_out, x2_2);
  not not_4 (not_4_out, x1_4);
  not not_5 (not_5_out, x3_5);
  and and_1 (and_1_out, not_1_out, x0, x0, x3);
  and and_2 (and_2_out, not_2_out, x2, x2, x1_2);
  and and_3 (and_3_out, x3_3, not_3_out, x1_3, x0_2);
  and and_4 (and_4_out, not_4_out, x0_3, x0_3, x3_4);
  and and_5 (and_5_out, not_5_out, x2_3, x2_3, x1_5);
  or or_1 (out_17, and_1_out, and_2_out, and_3_out);
  or or_2 (out_18, and_4_out, and_5_out);
endmodule

module Blatt_2_unisgned (
  input  x3,
  input  x2,
  input  x1,
  input  x0,
  output y0,
  output y3,
  output y2,
  output y1
);

  ROM #(.addrWidth(4), .dataWidth(1)) rom_1 (.addr({x3, x2, x1, x0}), .data(y0));  // open: sel
  ROM #(.addrWidth(4), .dataWidth(1)) rom_2 (.addr({x3, x2, x1, x0}), .data(y3));  // open: sel
  ROM #(.addrWidth(4), .dataWidth(1)) rom_3 (.addr({x3, x2, x1, x0}), .data(y2));  // open: sel
  ROM #(.addrWidth(4), .dataWidth(1)) rom_4 (.addr({x3, x2, x1, x0}), .data(y1));  // open: sel

  // Notes on the sheet:
  //   contents of rom_1 (hex, n*v repeats v):
  //   5*0 1 0 1 5*0 1 0 1
  //   contents of rom_2 (hex, n*v repeats v):
  //   15*0 1
  //   contents of rom_3 (hex, n*v repeats v):
  //   10*0 1 1 0 0 1
  //   contents of rom_4 (hex, n*v repeats v):
  //   6*0 1 1 0 1 0 1 0 1 1
endmodule

module Blatt_2_signed (
  input  x3,
  input  x2,
  input  x1,
  input  x0,
  output y0,
  output y1,
  output y2,
  output y3
);

  ROM #(.addrWidth(4), .dataWidth(1)) rom_1 (.addr({x3, x2, x1, x0}), .data(y0));  // open: sel
  ROM #(.addrWidth(4), .dataWidth(1)) rom_2 (.addr({x3, x2, x1, x0}), .data(y1));  // open: sel
  ROM #(.addrWidth(4), .dataWidth(1)) rom_3 (.addr({x3, x2, x1, x0}), .data(y2));  // open: sel
  ROM #(.addrWidth(4), .dataWidth(1)) rom_4 (.addr({x3, x2, x1, x0}), .data(y3));  // open: sel

  // Notes on the sheet:
  //   contents of rom_1 (hex, n*v repeats v):
  //   5*0 1 0 1 5*0 1 0 1
  //   contents of rom_2 (hex, n*v repeats v):
  //   6*0 1 1 0 1 0 1 0 1 1
  //   contents of rom_3 (hex, n*v repeats v):
  //   6*0 1 1 0 1 1 0 0 1
  //   contents of rom_4 (hex, n*v repeats v):
  //   6*0 1 1 0 1 0 0 0 1
endmodule

module Blatt_2_Aufgabe_2 (
  input  x3,
  input  x2,
  input  x1,
  input  x0,
  output y0
);

  ROM #(.addrWidth(4), .dataWidth(1)) rom_1 (.addr({x3, x2, x1, x0}), .data(y0));  // open: sel

  // Notes on the sheet:
  //   contents of rom_1 (hex, n*v repeats v):
  //   1 1 0 0 1 1 0 1 0 1 0 1 0 1 0 1
endmodule
