// Logisim project RA_neu.circ as structural Verilog: 9 circuits, main circuit Blatt_1_unsigned
module Blatt_1_unsigned (
  input  x2,
  input  x0,
  input  x3,
  input  x2_2,
  input  x1,
  input  x0_2,
  input  x3_2,
  input  x1_2,
  input  x0_3,
  input  x3_3,
  input  x0_4,
  input  x2_3,
  input  x2_4,
  input  x1_3,
  input  x3_4,
  input  x1_4,
  input  x0_5,
  input  x3_5,
  input  x1_5,
  input  x0_6,
  input  x3_6,
  input  x1_6,
  input  x2_5,
  output y0,
  output y3,
  output y1,
  output y2
);

  wire and_1_out, and_2_out, and_3_out, and_4_out, and_5_out, and_6_out, not_1_out, not_2_out, not_3_out,
       not_4_out, not_5_out, not_6_out;

  not not_1 (not_1_out, x2_3);
  not not_2 (not_2_out, x3_4);
  not not_3 (not_3_out, x0_5);
  not not_4 (not_4_out, x0_6);
  not not_5 (not_5_out, x2_5);
  not not_6 (not_6_out, x1_2);
  and and_1 (and_1_out, x3_2, not_6_out, x0_3);
  and and_2 (and_2_out, x3_3, x0_4, not_1_out);
  and and_3 (and_3_out, x2_4, x1_3, not_2_out);
  and and_4 (and_4_out, x1_4, not_3_out);
  and and_5 (and_5_out, x3_5, x1_5, not_4_out);
  and and_6 (and_6_out, x3_6, x1_6, not_5_out);
  or or_1 (y2, and_5_out, and_6_out);
  or or_2 (y1, and_1_out, and_2_out, and_3_out, and_4_out);
  and and_7 (y0, x2, x0);
  and and_8 (y3, x3, x2_2, x1, x0_2);
endmodule

module Blatt_1_signed (
  input  x1,
  input  x0,
  input  x3,
  input  x3_2,
  input  x2,
  input  x1_2,
  input  x3_3,
  input  x2_2,
  input  x1_3,
  input  x0_2,
  input  x1_4,
  input  x0_3,
  input  x3_4,
  input  x3_5,
  input  x2_3,
  input  x1_5,
  output out_17,
  output out_18
);

  wire and_1_out, and_2_out, and_3_out, and_4_out, and_5_out, not_1_out, not_2_out, not_3_out, not_4_out,
       not_5_out;

  not not_1 (not_1_out, x1);
  not not_2 (not_2_out, x3_2);
  not not_3 (not_3_out, x2_2);
  not not_4 (not_4_out, x1_4);
  not not_5 (not_5_out, x3_5);
  and and_1 (and_1_out, not_1_out, x0, x0, x3);
  and and_2 (and_2_out, not_2_out, x2, x2, x1_2);
  and and_3 (and_3_out, x3_3, not_3_out, x1_3, x0_2);
  and and_4 (and_4_out, not_4_out, x0_3, x0_3, x3_4);
  and and_5 (and_5_out, not_5_out, x2_3, x2_3, x1_5);
  or or_1 (out_17, and_1_out, and_2_out, and_3_out);
  or or_2 (out_18, and_4_out, and_5_out);
endmodule

module Blatt_2_unisgned (
  input  x3,
  input  x2,
  input  x1,
  input  x0,
  output y0,
  output y3,
  output y2,
  output y1
);

  ROM #(.addrWidth(4), .dataWidth(1)) rom_1 (.addr({x3, x2, x1, x0}), .data(y0));  // open: sel
  ROM #(.addrWidth(4), .dataWidth(1)) rom_2 (.addr({x3, x2, x1, x0}), .data(y3));  // open: sel
  ROM #(.addrWidth(4), .dataWidth(1)) rom_3 (.addr({x3, x2, x1, x0}), .data(y2));  // open: sel
  ROM #(.addrWidth(4), .dataWidth(1)) rom_4 (.addr({x3, x2, x1, x0}), .data(y1));  // open: sel

  // Notes on the sheet:
  //   contents of rom_1 (hex, n*v repeats v):
  //   5*0 1 0 1 5*0 1 0 1
  //   contents of rom_2 (hex, n*v repeats v):
  //   15*0 1
  //   contents of rom_3 (hex, n*v repeats v):
  //   10*0 1 1 0 0 1
  //   contents of rom_4 (hex, n*v repeats v):
  //   6*0 1 1 0 1 0 1 0 1 1
endmodule

module Blatt_2_signed (
  input  x3,
  input  x2,
  input  x1,
  input  x0,
  output y0,
  output y1,
  output y2,
  output y3
);

  ROM #(.addrWidth(4), .dataWidth(1)) rom_1 (.addr({x3, x2, x1, x0}), .data(y0));  // open: sel
  ROM #(.addrWidth(4), .dataWidth(1)) rom_2 (.addr({x3, x2, x1, x0}), .data(y1));  // open: sel
  ROM #(.addrWidth(4), .dataWidth(1)) rom_3 (.addr({x3, x2, x1, x0}), .data(y2));  // open: sel
  ROM #(.addrWidth(4), .dataWidth(1)) rom_4 (.addr({x3, x2, x1, x0}), .data(y3));  // open: sel

  // Notes on the sheet:
  //   contents of rom_1 (hex, n*v repeats v):
  //   5*0 1 0 1 5*0 1 0 1
  //   contents of rom_2 (hex, n*v repeats v):
  //   6*0 1 1 0 1 0 1 0 1 1
  //   contents of rom_3 (hex, n*v repeats v):
  //   6*0 1 1 0 1 1 0 0 1
  //   contents of rom_4 (hex, n*v repeats v):
  //   6*0 1 1 0 1 0 0 0 1
endmodule

module Blatt_2_Aufgabe_2 (
  input  x3,
  input  x2,
  input  x1,
  input  x0,
  output y0
);

  ROM #(.addrWidth(4), .dataWidth(1)) rom_1 (.addr({x3, x2, x1, x0}), .data(y0));  // open: sel

  // Notes on the sheet:
  //   contents of rom_1 (hex, n*v repeats v):
  //   1 1 0 0 1 1 0 1 0 1 0 1 0 1 0 1
endmodule

module Blatt_3 (
  output out_1,
  output out_2
);

  wire clock_1_out, clock_2_out, j_k_ff_1_q, j_k_ff_1_qn, j_k_ff_2_q;

  Clock clock_1 (.out(clock_1_out));
  Clock clock_2 (.out(clock_2_out));
  J_K_Flip_Flop j_k_ff_1 (
    .J(1'b1), .clk(clock_1_out), .K(1'b1), .Q(j_k_ff_1_q), .Qn(j_k_ff_1_qn));  // open: preset, en, reset
  J_K_Flip_Flop j_k_ff_2 (.J(1'b1), .clk(clock_2_out), .K(1'b1), .Q(j_k_ff_2_q));  // open: Qn, preset, en, reset
  J_K_Flip_Flop j_k_ff_3 (
    .J(j_k_ff_1_q), .clk(clock_1_out), .K(j_k_ff_1_qn), .Q(out_1));  // open: Qn, preset, en, reset
  J_K_Flip_Flop j_k_ff_4 (.J(1'b1), .clk(j_k_ff_2_q), .K(1'b1), .Q(out_2));  // open: Qn, preset, en, reset
endmodule

module Blatt_4_Aufgabe_1 (
  input  X,
  input  X_2,
  output y0,
  output y1,
  output y0_2,
  output y1_2
);

  wire and_1_out, and_2_out, and_3_out, and_4_out, and_5_out, and_6_out, and_7_out, and_8_out, and_9_out,
       and_10_out, and_11_out, and_12_out, and_13_out, and_14_out, and_15_out, clock_1_out, Clock_2_out,
       not_1_out, not_2_out, not_3_out, not_4_out, not_5_out, not_6_out, not_7_out, not_8_out, not_10_out,
       not_11_out, not_12_out, not_13_out, not_14_out, not_15_out, not_16_out, not_17_out, not_18_out,
       or_3_out, or_4_out, or_5_out, Z0_q, Z1_q, Z2_q;
  wire [3:1] d_ff_1_q;
  wire [4:2] rom_1_data;

  Clock clock_1 (.out(clock_1_out));
  D_Flip_Flop d_ff_1 (.clk(clock_1_out), .D(rom_1_data[2]), .Q(d_ff_1_q[1]));  // open: Qn, preset, en, reset
  D_Flip_Flop d_ff_2 (.clk(clock_1_out), .D(rom_1_data[3]), .Q(d_ff_1_q[2]));  // open: Qn, preset, en, reset
  D_Flip_Flop d_ff_3 (.clk(clock_1_out), .D(rom_1_data[4]), .Q(d_ff_1_q[3]));  // open: Qn, preset, en, reset
  ROM #(.addrWidth(4), .dataWidth(5)) rom_1 (.addr({d_ff_1_q, X_2}), .data({rom_1_data, y1, y0}));  // open: sel
  Clock Clock_2 (.out(Clock_2_out));
  D_Flip_Flop Z2 (.clk(Clock_2_out), .D(or_3_out), .Q(Z2_q));  // open: Qn, preset, en, reset
  D_Flip_Flop Z1 (.clk(Clock_2_out), .D(or_4_out), .Q(Z1_q));  // open: Qn, preset, en, reset
  D_Flip_Flop Z0 (.clk(Clock_2_out), .D(or_5_out), .Q(Z0_q));  // open: Qn, preset, en, reset
  not not_1 (not_1_out, Z2_q);
  not not_2 (not_2_out, Z0_q);
  not not_3 (not_3_out, Z2_q);
  not not_4 (not_4_out, Z0_q);
  not not_5 (not_5_out, Z2_q);
  not not_6 (not_6_out, Z1_q);
  not not_7 (not_7_out, X);
  not not_8 (not_8_out, Z0_q);
  // NOT_Gate not_9 has open pins: in=Z2_q, out=open
  not not_10 (not_10_out, X);
  not not_11 (not_11_out, Z0_q);
  not not_12 (not_12_out, Z1_q);
  not not_13 (not_13_out, X);
  not not_14 (not_14_out, Z2_q);
  not not_15 (not_15_out, Z1_q);
  not not_16 (not_16_out, Z2_q);
  not not_17 (not_17_out, Z0_q);
  not not_18 (not_18_out, Z0_q);
  and and_1 (and_1_out, Z0_q, Z1_q);
  and and_2 (and_2_out, not_1_out, Z1_q, not_2_out);
  and and_3 (and_3_out, Z1_q, Z0_q);
  and and_4 (and_4_out, Z2_q, Z0_q);
  and and_5 (and_5_out, Z2_q, Z1_q);
  and and_6 (and_6_out, not_3_out, Z1_q, not_4_out, X);
  and and_7 (and_7_out, not_5_out, not_6_out, Z0_q);
  and and_8 (and_8_out, Z1_q, Z0_q);
  and and_9 (and_9_out, Z2_q, Z0_q, X);
  and and_10 (and_10_out, not_7_out, not_8_out, Z1_q);
  and and_11 (and_11_out, not_10_out, Z2_q, not_11_out, not_12_out);
  and and_12 (and_12_out, not_13_out, Z0_q, Z1_q);
  and and_13 (and_13_out, not_14_out, not_15_out, X);
  and and_14 (and_14_out, not_16_out, not_17_out, X);
  and and_15 (and_15_out, Z1_q, not_18_out, X);
  or or_1 (y0_2, and_1_out, Z2_q);
  or or_2 (y1_2, and_2_out, and_3_out);
  or or_3 (or_3_out, and_4_out, and_5_out, and_6_out);
  or or_4 (or_4_out, and_7_out, and_8_out, and_9_out, and_10_out, and_11_out);
  or or_5 (or_5_out, and_12_out, and_13_out, and_14_out, and_15_out);

  // Notes on the sheet:
  //   contents of rom_1 (hex, n*v repeats v):
  //   0 4 8 c e 16 f 1 19 11 13 1b 15 11
endmodule

module Blatt_4_Aufgabe_2 (
  input  X,
  input  X_2,
  output y0,
  output y1,
  output Y0_2,
  output Y1_2
);

  wire and_2_out, and_3_out, and_4_out, and_5_out, and_6_out, and_7_out, clock_1_out, Clock_2_out, not_1_out,
       not_2_out, not_3_out, not_4_out, not_5_out, not_6_out, not_7_out, or_1_out, or_2_out, Z0_q, Z1_q;
  wire [3:1] d_ff_1_q;
  wire [4:2] rom_1_data;

  Clock clock_1 (.out(clock_1_out));
  Clock Clock_2 (.out(Clock_2_out));
  D_Flip_Flop d_ff_1 (.clk(clock_1_out), .D(rom_1_data[2]), .Q(d_ff_1_q[1]));  // open: Qn, preset, en, reset
  D_Flip_Flop Z0 (.clk(Clock_2_out), .D(or_2_out), .Q(Z0_q));  // open: Qn, preset, en, reset
  D_Flip_Flop Z1 (.clk(Clock_2_out), .D(or_1_out), .Q(Z1_q));  // open: Qn, preset, en, reset
  D_Flip_Flop Z2 (.clk(Clock_2_out), .D(and_2_out), .Q(Y0_2));  // open: Qn, preset, en, reset
  D_Flip_Flop d_ff_2 (.clk(clock_1_out), .D(rom_1_data[3]), .Q(d_ff_1_q[2]));  // open: Qn, preset, en, reset
  D_Flip_Flop d_ff_3 (.clk(clock_1_out), .D(rom_1_data[4]), .Q(d_ff_1_q[3]));  // open: Qn, preset, en, reset
  not not_1 (not_1_out, Z0_q);
  not not_2 (not_2_out, Z0_q);
  not not_3 (not_3_out, Z0_q);
  not not_4 (not_4_out, Z1_q);
  not not_5 (not_5_out, Y0_2);
  not not_6 (not_6_out, Z1_q);
  not not_7 (not_7_out, Z0_q);
  and and_1 (Y1_2, Z1_q, Z0_q, X_2);
  and and_2 (and_2_out, not_1_out, Z1_q, X_2);
  and and_3 (and_3_out, not_2_out, Z1_q, X_2);
  and and_4 (and_4_out, not_3_out, Y0_2, X_2);
  and and_5 (and_5_out, not_4_out, Z0_q, X_2);
  and and_6 (and_6_out, not_5_out, not_6_out, X_2);
  and and_7 (and_7_out, not_7_out, X_2, Z1_q);
  ROM #(.addrWidth(4), .dataWidth(5)) rom_1 (.addr({d_ff_1_q, X}), .data({rom_1_data, y1, y0}));  // open: sel
  or or_1 (or_1_out, and_3_out, and_4_out, and_5_out);
  or or_2 (or_2_out, and_6_out, and_7_out);

  // Notes on the sheet:
  //   contents of rom_1 (hex, n*v repeats v):
  //   0 4 8 4 e 10 0 2 8 1
endmodule

module Blatt_5 (
  input  in_1,
  input  in_2,
  input  in_3,
  input  in_4,
  input  in_5,
  output out_6,
  output out_7,
  output out_8,
  output out_9,
  output out_10,
  output out_11,
  output out_12
);

  wire and_1_out, and_2_out, and_3_out, clock_1_out;

  Clock clock_1 (.out(clock_1_out));
  J_K_Flip_Flop j_k_ff_1 (.J(and_1_out), .clk(in_3), .K(and_1_out), .Q(out_6));  // open: Qn, preset, en, reset
  J_K_Flip_Flop j_k_ff_2 (.J(out_8), .clk(in_3), .K(out_8), .Q(out_7));  // open: Qn, preset, en, reset
  J_K_Flip_Flop j_k_ff_3 (.J(in_1), .clk(in_3), .K(in_2), .Q(out_8));  // open: Qn, preset, en, reset
  J_K_Flip_Flop j_k_ff_4 (.J(in_4), .clk(clock_1_out), .K(in_5), .Q(out_12));  // open: Qn, preset, en, reset
  J_K_Flip_Flop j_k_ff_5 (.J(out_12), .clk(clock_1_out), .K(out_12), .Q(out_11));  // open: Qn, preset, en, reset
  and and_1 (and_1_out, out_7, out_8);
  and and_2 (and_2_out, out_12, out_11);
  J_K_Flip_Flop j_k_ff_6 (.J(and_2_out), .clk(clock_1_out), .K(and_2_out), .Q(out_10));  // open: Qn, preset, en, reset
  and and_3 (and_3_out, out_10, and_2_out);
  J_K_Flip_Flop j_k_ff_7 (.J(and_3_out), .clk(clock_1_out), .K(and_3_out), .Q(out_9));  // open: Qn, preset, en, reset
endmodule
